# Fritzing sketch Lampada Colorata (saved by Fritzing 0.9.3b)
breadboards: 1

parts:
  Componente1 = Arduino Uno (Rev3)
  LED1 = RGB LED (com. cathode, rgb) [package="5 mm [THT]"]
  R1 = Resistor [tolerance=±5% resistance=220 package=THT]
  R2 = Resistor [tolerance=±5% resistance=220 package=THT]
  R3 = Resistor [tolerance=±5% resistance=220 package=THT]
  R4 = Rotary Potentiometer (Small) [maximum_resistance=100kΩ package=THT]
  S1 = Pushbutton [package="[THT]"]
  S2 = Pushbutton [package="[THT]"]
  S3 = Pushbutton [package="[THT]"]
  R5 = Resistor [tolerance=±5% resistance=220 package=THT]
  R6 = Resistor [tolerance=±5% resistance=220 package=THT]
  R7 = Resistor [tolerance=±5% resistance=220 package=THT]

nets:
  N1: Componente1.D9_PWM, R3.Pin_0
  N2: Componente1.D10_PWM/SS, R2.Pin_0
  N3: Componente1.D11_PWM/MOSI, R1.Pin_0
  N4: Componente1.5V, R4.leg1, S1.Pin_1, S1.Pin_2, S2.Pin_1, S2.Pin_2, S3.Pin_1, S3.Pin_2
  N5: Componente1.GND, LED1.common_cathode, R4.leg2, R5.Pin_0, R6.Pin_0, R7.Pin_0
  N6: LED1.red_anode, R1.Pin_1
  N7: LED1.green_anode, R2.Pin_1
  N8: LED1.blue_anode, R3.Pin_1
  N9: S1.Pin_3, S1.Pin_4, R5.Pin_1
  N10: S2.Pin_3, S2.Pin_4, R6.Pin_1
  N11: S3.Pin_3, S3.Pin_4, R7.Pin_1
